// Logisim project SFQ.circ as structural Verilog
module main (
  input  in_1,
  input  in_2,
  input  in_3,
  output out_4
);

  wire clk_nand_1_out_4, clock_1_out, clock_2_out, clock_3_out, d_ff_1_q, d_ff_2_q, d_ff_3_q, d_ff_4_q,
       d_ff_5_q, d_ff_6_q, d_ff_7_q, d_ff_8_q;
  wire [1:0] counter_1_q;
  wire [3:0] d_ff_9_q, rom_1_data;

  Counter #(.width(2), .max('h3)) counter_1 (.Q(counter_1_q), .clk(clock_1_out));  // open: load, D, count, carry, clr
  Clock #(.highDuration(3), .lowDuration(3)) clock_1 (.out(clock_1_out));
  CLK_NAND clk_nand_1 (.in_1(in_1), .in_2(in_2), .in_3(in_3), .out_4(clk_nand_1_out_4));
  CLK_AND clk_and_1 ();  // open: in_2, in_3, out_4, in_1
  ROM #(.addrWidth(2), .dataWidth(4)) rom_1 (.addr(counter_1_q), .data(rom_1_data));  // open: sel
  CLK_OR clk_or_1 (.in_1(in_1), .in_2(clk_nand_1_out_4), .out_4(out_4));  // open: in_3
  Clock #(.highDuration(3), .lowDuration(3)) clock_2 (.out(clock_2_out));
  D_Flip_Flop d_ff_1 (.clk(clock_2_out), .D(rom_1_data[0]), .Q(d_ff_1_q));  // open: Qn, preset, en, reset
  D_Flip_Flop d_ff_2 (.clk(clock_2_out), .D(rom_1_data[1]), .Q(d_ff_2_q));  // open: Qn, preset, en, reset
  D_Flip_Flop d_ff_3 (.clk(clock_2_out), .D(rom_1_data[2]), .Q(d_ff_3_q));  // open: Qn, preset, en, reset
  D_Flip_Flop d_ff_4 (.clk(clock_2_out), .D(rom_1_data[3]), .Q(d_ff_4_q));  // open: Qn, preset, en, reset
  Clock #(.highDuration(2), .lowDuration(2)) clock_3 (.out(clock_3_out));
  D_Flip_Flop d_ff_5 (.clk(clock_3_out), .D(d_ff_1_q), .Q(d_ff_5_q));  // open: Qn, preset, en, reset
  D_Flip_Flop d_ff_6 (.clk(clock_3_out), .D(d_ff_2_q), .Q(d_ff_6_q));  // open: Qn, preset, en, reset
  D_Flip_Flop d_ff_7 (.clk(clock_3_out), .D(d_ff_3_q), .Q(d_ff_7_q));  // open: Qn, preset, en, reset
  D_Flip_Flop d_ff_8 (.clk(clock_3_out), .D(d_ff_4_q), .Q(d_ff_8_q));  // open: Qn, preset, en, reset
  D_Flip_Flop d_ff_9 (.clk(clock_3_out), .D(d_ff_5_q), .Q(d_ff_9_q[0]));  // open: Qn, preset, en, reset
  D_Flip_Flop d_ff_10 (.clk(clock_3_out), .D(d_ff_6_q), .Q(d_ff_9_q[1]));  // open: Qn, preset, en, reset
  D_Flip_Flop d_ff_11 (.clk(clock_3_out), .D(d_ff_7_q), .Q(d_ff_9_q[2]));  // open: Qn, preset, en, reset
  D_Flip_Flop d_ff_12 (.clk(clock_3_out), .D(d_ff_8_q), .Q(d_ff_9_q[3]));  // open: Qn, preset, en, reset

  // Notes on the sheet:
  //   contents of rom_1 (hex, n*v repeats v):
  //   7 2 4 1
endmodule

module CLK_AND (
  input  in_1,
  input  in_2,
  input  in_3,
  output out_4
);

  wire d_ff_1_q, d_ff_2_q;

  D_Flip_Flop d_ff_1 (.clk(in_1), .D(in_2), .Q(d_ff_1_q));  // open: Qn, preset, en, reset
  D_Flip_Flop d_ff_2 (.clk(in_1), .D(in_3), .Q(d_ff_2_q));  // open: Qn, preset, en, reset
  and and_1 (out_4, d_ff_1_q, d_ff_2_q);
endmodule

module CLK_NAND (
  input  in_1,
  input  in_2,
  input  in_3,
  output out_4
);

  wire d_ff_1_q, d_ff_2_q;

  D_Flip_Flop d_ff_1 (.clk(in_1), .D(in_2), .Q(d_ff_1_q));  // open: Qn, preset, en, reset
  D_Flip_Flop d_ff_2 (.clk(in_1), .D(in_3), .Q(d_ff_2_q));  // open: Qn, preset, en, reset
  nand nand_1 (out_4, d_ff_1_q, d_ff_2_q);
endmodule

module CLK_OR (
  input  in_1,
  input  in_2,
  input  in_3,
  output out_4
);

  wire d_ff_1_q, d_ff_2_q;

  D_Flip_Flop d_ff_1 (.clk(in_1), .D(in_2), .Q(d_ff_1_q));  // open: Qn, preset, en, reset
  D_Flip_Flop d_ff_2 (.clk(in_1), .D(in_3), .Q(d_ff_2_q));  // open: Qn, preset, en, reset
  or or_1 (out_4, d_ff_1_q, d_ff_2_q);
endmodule

module CLK_NOR (
  input  in_1,
  input  in_2,
  input  in_3,
  output out_4
);

  wire d_ff_1_q, d_ff_2_q;

  D_Flip_Flop d_ff_1 (.clk(in_1), .D(in_2), .Q(d_ff_1_q));  // open: Qn, preset, en, reset
  D_Flip_Flop d_ff_2 (.clk(in_1), .D(in_3), .Q(d_ff_2_q));  // open: Qn, preset, en, reset
  nor nor_1 (out_4, d_ff_1_q, d_ff_2_q);
endmodule
